// Logisim project cas369_lab7.circ as structural Verilog: 1 circuit, main circuit main
module main (
  input  [3:0] A,
  input  [3:0] B,
  input  sub
);

  wire adder_1_cout, and_1_out, SOV, UOV;
  wire [3:0] multiplexer_1_out, not_1_p2, O;

  // NOT_Gate #(.width(4)) not_1: pin names not known; wires that end beside it: B, not_1_p2
  Multiplexer #(.width(4)) multiplexer_1 (.in0(B), .in1(not_1_p2), .out(multiplexer_1_out), .sel(sub));  // open: en
  Adder #(.width(4)) adder_1 (.a(A), .b(multiplexer_1_out), .out(O), .cin(sub), .cout(adder_1_cout));
  xor xor_1 (UOV, adder_1_cout, sub);
  // Probe on A
  // Probe on B
  // Probe on O
  LED led_1 (.in(UOV));
  // Probe on A
  // Probe on B
  // Probe on O
  LED led_2 (.in(SOV));
  and and_1 (and_1_out, A[3], multiplexer_1_out[3]);
  xor xor_2 (SOV, and_1_out, O[3]);
endmodule
