// Logisim project cas369_lab8.circ as structural Verilog: 3 circuits, main circuit main
module main (
  input  MemWrite,
  input  RegWrite,
  input  [1:0] rd,
  input  [7:0] in_4,
  input  [1:0] rs,
  input  ALUSrc,
  input  [7:0] in_7,
  input  [7:0] in_8,
  input  [1:0] rt,
  input  [7:0] in_10,
  input  [1:0] ALUOp,
  input  [7:0] in_12,
  input  [15:0] Imm,
  input  RegDataSrc
);

  wire button_1_out, clk, clock_1_out;
  wire [31:0] alu_1_out, bit_extender_1_out, multiplexer_1_out, multiplexer_2_out, ram_1_data,
       reg_file_1_rs_out, reg_file_1_rt_out;

  Clock clock_1 (.out(clock_1_out));
  or or_1 (clk, clock_1_out, button_1_out);
  Button button_1 (.out(button_1_out));
  Multiplexer #(.width(32)) multiplexer_1 (
    .in0(alu_1_out), .in1(ram_1_data), .out(multiplexer_1_out), .sel(RegDataSrc));  // open: en
  Reg_File reg_file_1 (
    .Data(multiplexer_1_out), .WE(RegWrite), .CLK(clk), .rs_out(reg_file_1_rs_out),
    .rt_out(reg_file_1_rt_out), .rd(rd), .rs(rs), .rt(rt));
  assign bit_extender_1_out = {{16{Imm[15]}}, Imm};  // Bit_Extender bit_extender_1
  Multiplexer #(.width(32)) multiplexer_2 (
    .in0(reg_file_1_rt_out), .in1(bit_extender_1_out), .out(multiplexer_2_out), .sel(ALUSrc));  // open: en
  ALU alu_1 (.A(reg_file_1_rs_out), .B(multiplexer_2_out), .Out(alu_1_out), .ALUOp(ALUOp));
  RAM #(.dataWidth(32), .bus("separate")) ram_1 (
    .addr(alu_1_out[9:2]), .din(reg_file_1_rt_out), .data(ram_1_data), .clk(MemWrite));  // open: str, sel, ld, clr

  // Other names for the same wires on the sheet: alu_out[7:0] = in_10; imm_t[7:0] = in_8; mem_out[7:0] = in_12;
  //   rs_out[7:0] = in_4; rt_out[7:0] = in_7

  // Notes on the sheet:
  //   -----------------------------
  //   directly from instruction fields
endmodule

module ALU (
  input  [31:0] A,
  input  [31:0] B,
  input  [1:0] ALUOp,
  output [31:0] Out
);

  wire [31:0] adder_1_out, and_1_out, or_1_p3, subtractor_1_out;

  // Probe on A
  Adder #(.width(32)) adder_1 (.a(A), .b(B), .out(adder_1_out));  // open: cin, cout
  Subtractor #(.width(32)) subtractor_1 (.a(A), .b(B), .out(subtractor_1_out));  // open: bin, bout
  assign and_1_out = A & B;  // AND_Gate and_1, 32 bits wide
  // OR_Gate #(.width(32)) or_1: pin names not known; wires that end beside it: A, B, or_1_p3
  // Probe on B
  Multiplexer #(.select(2), .width(32)) multiplexer_1 (
    .in0(adder_1_out), .in1(subtractor_1_out), .in2(and_1_out), .in3(or_1_p3), .out(Out), .sel(ALUOp));  // open: en

  // Notes on the sheet:
  //   0 = +
  //   1 = -
  //   2 = &
  //   3 = |
endmodule

module Reg_File (
  input  [31:0] Data,
  input  [1:0] rs,
  input  WE,
  input  CLK,
  input  [1:0] rd,
  input  [1:0] rt,
  output [31:0] rs_out,
  output [31:0] rt_out
);

  wire demultiplexer_1_out0, demultiplexer_1_out1, demultiplexer_1_out2, demultiplexer_1_out3;
  wire [31:0] _1__at_q, _2__v0_q, _3__v1_q;

  Demultiplexer #(.select(2)) demultiplexer_1 (
    .out0(demultiplexer_1_out0), .out1(demultiplexer_1_out1), .out2(demultiplexer_1_out2),
    .out3(demultiplexer_1_out3), .in(WE), .sel(rd));  // open: en
  Register #(.width(32)) _1__at (.D(Data), .en(demultiplexer_1_out1), .Q(_1__at_q), .clk(CLK));  // open: clr
  Register #(.width(32)) _2__v0 (.D(Data), .en(demultiplexer_1_out2), .Q(_2__v0_q), .clk(CLK));  // open: clr
  Register #(.width(32)) _3__v1 (.D(Data), .en(demultiplexer_1_out3), .Q(_3__v1_q), .clk(CLK));  // open: clr
  Multiplexer #(.select(2), .width(32)) multiplexer_1 (
    .in0({32{1'b0}}), .in1(_1__at_q), .in2(_2__v0_q), .in3(_3__v1_q), .out(rs_out), .sel(rs));  // open: en
  Multiplexer #(.select(2), .width(32)) multiplexer_2 (
    .in0({32{1'b0}}), .in1(_1__at_q), .in2(_2__v0_q), .in3(_3__v1_q), .out(rt_out), .sel(rt));  // open: en

  // Notes on the sheet:
  //   really should be using
  //   more tunnels here, huh?
  //   why don't you try
  //   cleaning it up?
  //   etc... until 31 (ra)
  //   0 (zero)
endmodule
